// Logisim project 2_bit_logic_unit.circ as structural Verilog: 1 circuit, main circuit main
module main (
  input  A1,
  input  B1,
  input  Enable,
  input  A2,
  input  B2,
  input  [1:0] S,
  output F1,
  output F2
);

  wire and_1_out, and_2_out, not_1_out, not_2_out, or_1_out, or_2_out, xor_1_out, xor_2_out;

  and and_1 (and_1_out, A1, B1);
  or or_1 (or_1_out, A1, B1);
  not not_1 (not_1_out, A1);
  xor xor_1 (xor_1_out, A1, B1);
  and and_2 (and_2_out, A2, B2);
  or or_2 (or_2_out, A2, B2);
  xor xor_2 (xor_2_out, A2, B2);
  not not_2 (not_2_out, A2);
  Multiplexer #(.enable("true"), .select(2)) multiplexer_1 (
    .in0(and_1_out), .in1(or_1_out), .in2(xor_1_out), .in3(not_1_out), .out(F1), .sel(S), .en(Enable));
  Multiplexer #(.enable("true"), .select(2)) multiplexer_2 (
    .in0(and_2_out), .in1(or_2_out), .in2(xor_2_out), .in3(not_2_out), .out(F2), .sel(S), .en(Enable));

  // Notes on the sheet:
  //   Selectors
  //   AND Gate
  //   OR Gate
  //   NOT Gate
  //   AND Gate
  //   XOR Gate
  //   OR Gate
  //   XOR Gate
  //   NOT Gate
endmodule
