// Logisim project 4_bit_arithmetic_unit.circ as structural Verilog: 1 circuit, main circuit main
module main (
  input  Cin,
  input  [1:0] S,
  input  A0,
  input  B0,
  input  A1,
  input  B1,
  input  A2,
  input  B2,
  input  A3,
  input  B3,
  input  _0,
  input  Enable,
  output D0,
  output D1,
  output D2,
  output D3,
  output Carry
);

  wire adder_1_cout, adder_2_cout, adder_3_cout, multiplexer_1_out, multiplexer_2_out, multiplexer_4_out,
       multiplexer_5_out, not_1_out, not_2_out, not_3_out, not_4_out, not_5_out;

  not not_1 (not_1_out, B0);
  not not_2 (not_2_out, B1);
  not not_3 (not_3_out, B2);
  not not_4 (not_4_out, B3);
  not not_5 (not_5_out, _0);
  Multiplexer #(.select(2)) multiplexer_1 (
    .in0(B0), .in1(not_1_out), .in2(_0), .in3(not_5_out), .out(multiplexer_1_out), .sel(S));
  Multiplexer #(.enable("true"), .select(2)) multiplexer_2 (
    .in0(B1), .in1(not_2_out), .in2(_0), .in3(not_5_out), .out(multiplexer_2_out), .sel(S), .en(Enable));
  Multiplexer #(.enable("true"), .select(2)) multiplexer_3 (
    .in0(B1), .in1(not_2_out), .in2(_0), .in3(not_5_out), .out(multiplexer_2_out), .sel(S), .en(Enable));
  Multiplexer #(.enable("true"), .select(2)) multiplexer_4 (
    .in0(B2), .in1(not_3_out), .in2(_0), .in3(not_5_out), .out(multiplexer_4_out), .sel(S), .en(Enable));
  Multiplexer #(.enable("true"), .select(2)) multiplexer_5 (
    .in0(B3), .in1(not_4_out), .in2(_0), .in3(not_5_out), .out(multiplexer_5_out), .sel(S), .en(Enable));
  Adder #(.width(1)) adder_1 (.a(A0), .b(multiplexer_1_out), .out(D0), .cin(Cin), .cout(adder_1_cout));
  Adder #(.width(1)) adder_2 (.a(A1), .b(multiplexer_2_out), .out(D1), .cin(adder_1_cout), .cout(adder_2_cout));
  Adder #(.width(1)) adder_3 (.a(A2), .b(multiplexer_4_out), .out(D2), .cin(adder_2_cout), .cout(adder_3_cout));
  Adder #(.width(1)) adder_4 (.a(A3), .b(multiplexer_5_out), .out(D3), .cin(adder_3_cout), .cout(Carry));

  // Notes on the sheet:
  //   1
endmodule
