// Logisim project 4_bit_multiplier.circ as structural Verilog: 3 circuits, main circuit main
module main (
  input  B4,
  input  B3,
  input  B2,
  input  B1,
  input  A4,
  input  A3,
  input  A2,
  input  A1,
  input  in_9,
  input  in_10,
  output S8,
  output S7,
  output S6,
  output S5,
  output S4,
  output S3,
  output S2,
  output S1
);

  wire adder_circuit_1_cout, adder_circuit_1_sum2, adder_circuit_1_sum3, adder_circuit_1_sum4,
       adder_circuit_2_cout, adder_circuit_2_sum2, adder_circuit_2_sum3, adder_circuit_2_sum4, and_7400_1_c6,
       and_7400_1_c8, and_7400_1_c11, and_7400_2_c3, and_7400_2_c6, and_7400_2_c8, and_7400_2_c11,
       and_7400_3_c3, and_7400_3_c6, and_7400_3_c8, and_7400_3_c11, and_7400_4_c3, and_7400_4_c6,
       and_7400_4_c8, and_7400_4_c11;

  and_7400 and_7400_1 (
    .A1(A1), .B2(B1), .A4(A1), .B5(B2), .A13(A1), .B12(A3), .A10(A1), .B9(B4), .C3(S1), .C6(and_7400_1_c6),
    .C11(and_7400_1_c11), .C8(and_7400_1_c8));
  and_7400 and_7400_2 (
    .A1(A2), .B2(B1), .A4(A2), .B5(B2), .A13(A2), .B12(A3), .A10(A2), .B9(B4), .C3(and_7400_2_c3),
    .C6(and_7400_2_c6), .C11(and_7400_2_c11), .C8(and_7400_2_c8));
  and_7400 and_7400_3 (
    .A1(A3), .B2(B1), .A4(A3), .B5(B2), .A13(A3), .B12(A3), .A10(A3), .B9(B4), .C3(and_7400_3_c3),
    .C6(and_7400_3_c6), .C11(and_7400_3_c11), .C8(and_7400_3_c8));
  and_7400 and_7400_4 (
    .A1(A4), .B2(B1), .A4(A4), .B5(B2), .A13(A4), .B12(A3), .A10(A4), .B9(B4), .C3(and_7400_4_c3),
    .C6(and_7400_4_c6), .C11(and_7400_4_c11), .C8(and_7400_4_c8));
  adder_circuit adder_circuit_1 (
    .B1(and_7400_2_c3), .Cin(in_9), .A2(and_7400_1_c11), .B2(and_7400_2_c6), .A3(and_7400_1_c8),
    .B3(and_7400_2_c11), .A4(in_10), .A1(and_7400_1_c6), .B4(and_7400_2_c8), .Cout(adder_circuit_1_cout),
    .Sum1(S2), .Sum2(adder_circuit_1_sum2), .Sum3(adder_circuit_1_sum3), .Sum4(adder_circuit_1_sum4));
  adder_circuit adder_circuit_2 (
    .B1(and_7400_3_c3), .Cin(in_9), .A2(adder_circuit_1_sum3), .B2(and_7400_3_c6), .A3(adder_circuit_1_sum4),
    .B3(and_7400_3_c11), .A4(adder_circuit_1_cout), .A1(adder_circuit_1_sum2), .B4(and_7400_3_c8),
    .Cout(adder_circuit_2_cout), .Sum1(S3), .Sum2(adder_circuit_2_sum2), .Sum3(adder_circuit_2_sum3),
    .Sum4(adder_circuit_2_sum4));
  adder_circuit adder_circuit_3 (
    .B1(and_7400_4_c3), .Cin(in_9), .A2(adder_circuit_2_sum3), .B2(and_7400_4_c6), .A3(adder_circuit_2_sum4),
    .B3(and_7400_4_c11), .A4(adder_circuit_2_cout), .A1(adder_circuit_2_sum2), .B4(and_7400_4_c8), .Cout(S8),
    .Sum1(S4), .Sum2(S5), .Sum3(S6), .Sum4(S7));

  assign B3 = A3;
endmodule

module and_7400 (
  input  A1,
  input  B2,
  input  A4,
  input  B5,
  input  A13,
  input  B12,
  input  A10,
  input  B9,
  output C3,
  output C6,
  output C11,
  output C8
);

  and and_1 (C3, A1, B2);
  and and_2 (C6, A4, B5);
  and and_3 (C11, A13, B12);
  and and_4 (C8, A10, B9);
endmodule

module adder_circuit (
  input  A1,
  input  B1,
  input  Cin,
  input  A2,
  input  B2,
  input  A3,
  input  B3,
  input  A4,
  input  B4,
  output Sum1,
  output Sum2,
  output Sum3,
  output Sum4,
  output Cout
);

  wire and_1_out, and_2_out, and_3_out, and_4_out, and_5_out, and_6_out, and_7_out, and_8_out, or_1_out,
       or_2_out, or_3_out, xor_1_out, xor_2_out, xor_3_out, xor_4_out;

  xor xor_1 (xor_1_out, A1, B1);
  and and_1 (and_1_out, A1, B1);
  xor xor_2 (xor_2_out, A2, B2);
  and and_2 (and_2_out, A2, B2);
  xor xor_3 (xor_3_out, A3, B3);
  and and_3 (and_3_out, A3, B3);
  xor xor_4 (xor_4_out, A4, B4);
  and and_4 (and_4_out, A4, B4);
  and and_5 (and_5_out, xor_1_out, Cin);
  and and_6 (and_6_out, xor_2_out, or_1_out);
  and and_7 (and_7_out, xor_3_out, or_2_out);
  and and_8 (and_8_out, xor_4_out, or_3_out);
  xor xor_5 (Sum1, xor_1_out, Cin);
  or or_1 (or_1_out, and_5_out, and_1_out);
  xor xor_6 (Sum2, xor_2_out, or_1_out);
  or or_2 (or_2_out, and_6_out, and_2_out);
  xor xor_7 (Sum3, xor_3_out, or_2_out);
  or or_3 (or_3_out, and_7_out, and_3_out);
  xor xor_8 (Sum4, xor_4_out, or_3_out);
  or or_4 (Cout, and_8_out, and_4_out);
endmodule
