// Logisim project R-type-datapath-with-ALU.circ as structural Verilog
module register_file (
  input  [3:0] Read_register1,
  input  [3:0] Read_Register2,
  input  [15:0] Data_Input,
  input  [3:0] Write_register,
  input  Write_Enable,
  input  Clock,
  output [15:0] Read_data1,
  output [15:0] Read_Data2
);

  wire and_1_out, and_2_out, and_3_out, and_4_out, and_5_out, and_6_out, and_7_out, and_8_out, and_9_out,
       and_10_out, and_11_out, and_12_out, and_13_out, and_14_out, and_15_out, and_16_out, decoder_1_out0,
       decoder_1_out1, decoder_1_out2, decoder_1_out3, decoder_1_out4, decoder_1_out5, decoder_1_out6,
       decoder_1_out7, decoder_1_out8, decoder_1_out9, decoder_1_out10, decoder_1_out11, decoder_1_out12,
       decoder_1_out13, decoder_1_out14, decoder_1_out15;
  wire [15:0] R0_q, R1_q, R2_q, register_1_q, register_2_q, register_3_q, register_4_q, register_5_q,
       register_6_q, register_7_q, register_8_q, register_9_q, register_10_q, register_11_q, register_12_q,
       register_13_q;

  Decoder #(.select(4)) decoder_1 (
    .out0(decoder_1_out0), .out1(decoder_1_out1), .out2(decoder_1_out2), .out3(decoder_1_out3),
    .out4(decoder_1_out4), .out5(decoder_1_out5), .out6(decoder_1_out6), .out7(decoder_1_out7),
    .out8(decoder_1_out8), .out9(decoder_1_out9), .out10(decoder_1_out10), .out11(decoder_1_out11),
    .out12(decoder_1_out12), .out13(decoder_1_out13), .out14(decoder_1_out14), .out15(decoder_1_out15),
    .sel(Write_register));  // open: en
  and and_1 (and_1_out, decoder_1_out0, Write_Enable);
  and and_2 (and_2_out, decoder_1_out1, Write_Enable);
  and and_3 (and_3_out, decoder_1_out2, Write_Enable);
  and and_4 (and_4_out, decoder_1_out3, Write_Enable);
  and and_5 (and_5_out, decoder_1_out4, Write_Enable);
  and and_6 (and_6_out, decoder_1_out5, Write_Enable);
  and and_7 (and_7_out, decoder_1_out6, Write_Enable);
  and and_8 (and_8_out, decoder_1_out7, Write_Enable);
  and and_9 (and_9_out, decoder_1_out8, Write_Enable);
  and and_10 (and_10_out, decoder_1_out9, Write_Enable);
  and and_11 (and_11_out, decoder_1_out10, Write_Enable);
  and and_12 (and_12_out, decoder_1_out11, Write_Enable);
  and and_13 (and_13_out, decoder_1_out12, Write_Enable);
  and and_14 (and_14_out, decoder_1_out13, Write_Enable);
  and and_15 (and_15_out, decoder_1_out14, Write_Enable);
  and and_16 (and_16_out, decoder_1_out15, Write_Enable);
  Register #(.width(16)) R0 (.D(Data_Input), .en(and_1_out), .Q(R0_q), .clk(Clock));  // open: clr
  Register #(.width(16)) R1 (.D(Data_Input), .en(and_2_out), .Q(R1_q), .clk(Clock));  // open: clr
  Register #(.width(16)) R2 (.D(Data_Input), .en(and_3_out), .Q(R2_q), .clk(Clock));  // open: clr
  Register #(.width(16)) register_1 (.D(Data_Input), .en(and_4_out), .Q(register_1_q), .clk(Clock));  // open: clr
  Register #(.width(16)) register_2 (.D(Data_Input), .en(and_5_out), .Q(register_2_q), .clk(Clock));  // open: clr
  Register #(.width(16)) register_3 (.D(Data_Input), .en(and_6_out), .Q(register_3_q), .clk(Clock));  // open: clr
  Register #(.width(16)) register_4 (.D(Data_Input), .en(and_7_out), .Q(register_4_q), .clk(Clock));  // open: clr
  Register #(.width(16)) register_5 (.D(Data_Input), .en(and_8_out), .Q(register_5_q), .clk(Clock));  // open: clr
  Register #(.width(16)) register_6 (.D(Data_Input), .en(and_9_out), .Q(register_6_q), .clk(Clock));  // open: clr
  Register #(.width(16)) register_7 (.D(Data_Input), .en(and_10_out), .Q(register_7_q), .clk(Clock));  // open: clr
  Register #(.width(16)) register_8 (.D(Data_Input), .en(and_11_out), .Q(register_8_q), .clk(Clock));  // open: clr
  Register #(.width(16)) register_9 (.D(Data_Input), .en(and_12_out), .Q(register_9_q), .clk(Clock));  // open: clr
  Register #(.width(16)) register_10 (.D(Data_Input), .en(and_13_out), .Q(register_10_q), .clk(Clock));  // open: clr
  Register #(.width(16)) register_11 (.D(Data_Input), .en(and_14_out), .Q(register_11_q), .clk(Clock));  // open: clr
  Register #(.width(16)) register_12 (.D(Data_Input), .en(and_15_out), .Q(register_12_q), .clk(Clock));  // open: clr
  Register #(.width(16)) register_13 (.D(Data_Input), .en(and_16_out), .Q(register_13_q), .clk(Clock));  // open: clr
  Multiplexer #(.select(4), .width(16)) multiplexer_1 (
    .in0(R0_q), .in1(R1_q), .in2(R2_q), .in3(register_1_q), .in4(register_2_q), .in5(register_3_q),
    .in6(register_4_q), .in7(register_5_q), .in8(register_6_q), .in9(register_7_q), .in10(register_8_q),
    .in11(register_9_q), .in12(register_10_q), .in13(register_11_q), .in14(register_12_q),
    .in15(register_13_q), .out(Read_Data2), .sel(Read_Register2));
  Multiplexer #(.select(4), .width(16)) multiplexer_2 (
    .in0(R0_q), .in1(R1_q), .in2(R2_q), .in3(register_1_q), .in4(register_2_q), .in5(register_3_q),
    .in6(register_4_q), .in7(register_5_q), .in8(register_6_q), .in9(register_7_q), .in10(register_8_q),
    .in11(register_9_q), .in12(register_10_q), .in13(register_11_q), .in14(register_12_q),
    .in15(register_13_q), .out(Read_data1), .sel(Read_register1));
endmodule

module r_type_data_path (
  input  in_1,
  input  [2:0] ALUOP,
  input  BIN,
  input  Write_enable,
  output [15:0] READ_DATA1,
  output [3:0] OPCode,
  output [3:0] Read_reg1,
  output [3:0] Read_reg2,
  output [15:0] RESULT,
  output [3:0] Write_reg,
  output oVERFLOW,
  output [15:0] READ_DATA2
);

  wire clk_out;
  wire [15:0] adder_1_out, register_1_q;

  Clock clk (.out(clk_out));
  Register #(.width(16)) register_1 (.D(adder_1_out), .Q(register_1_q), .clk(clk_out));  // open: en, clr
  ROM #(.addrWidth(16), .dataWidth(16)) rom_1 (.addr(register_1_q), .data({OPCode, Read_reg1, Read_reg2, Write_reg}));
  Adder #(.width(16)) adder_1 (.a(register_1_q), .b(16'h1), .out(adder_1_out));  // open: cin, cout
  register_file register_file_1 (
    .Read_data1(READ_DATA1), .Read_Data2(READ_DATA2), .Write_Enable(Write_enable),
    .Write_register(Write_reg), .Read_register1(Read_reg1), .Data_Input(RESULT), .Read_Register2(Read_reg2),
    .Clock(clk_out));
  ALU alu_1 (.Cin(in_1), .B(READ_DATA2), .A(READ_DATA1), .Bin(BIN), .ALUOP(ALUOP), .Result(RESULT), .Cout(oVERFLOW));

  // Notes on the sheet:
  //   contents of rom_1 (hex, n*v repeats v):
  //   431
endmodule

module ALU (
  input  Cin,
  input  [15:0] B,
  input  [15:0] A,
  input  Bin,
  input  [2:0] ALUOP,
  output [15:0] Result,
  output Cout
);

  wire [15:0] adder_1_out, and_1_out, multiplexer_1_out, nand_1_out, not_1_out, or_1_out, xnor_1_out,
       xor_1_out;

  assign not_1_out = ~B;  // NOT_Gate not_1, 16 bits wide
  Multiplexer #(.width(16)) multiplexer_1 (.in0(B), .in1(not_1_out), .out(multiplexer_1_out), .sel(Bin));
  assign and_1_out = A & B;  // AND_Gate and_1, 16 bits wide
  assign or_1_out = A | B;  // OR_Gate or_1, 16 bits wide
  Adder #(.width(16)) adder_1 (.a(A), .b(multiplexer_1_out), .out(adder_1_out), .cin(Cin), .cout(Cout));
  assign xor_1_out = A ^ B;  // XOR_Gate xor_1, 16 bits wide
  assign nand_1_out = ~(A & B);  // NAND_Gate nand_1, 16 bits wide
  assign xnor_1_out = ~(A ^ B);  // XNOR_Gate xnor_1, 16 bits wide
  Multiplexer #(.select(3), .width(16)) multiplexer_2 (
    .in0(and_1_out), .in1(or_1_out), .in2(adder_1_out), .in3(xor_1_out), .in4(nand_1_out), .in5(xnor_1_out),
    .out(Result), .sel(ALUOP));  // open: in6, in7
endmodule
