// Logisim project pipelined_datapath.circ as structural Verilog: 17 circuits, main circuit AND_7408
module AND_7408 (
  input  in_1,
  input  in_2,
  input  in_3,
  input  in_4,
  input  in_5,
  input  in_6,
  input  in_7,
  input  in_8,
  output out_9,
  output out_10,
  output out_11,
  output out_12
);

  and and_1 (out_9, in_1, in_2);
  and and_2 (out_10, in_3, in_4);
  and and_3 (out_11, in_5, in_6);
  and and_4 (out_12, in_7, in_8);
endmodule

module OR_7432 (
  input  in_1,
  input  in_2,
  input  in_3,
  input  in_4,
  input  in_5,
  input  in_6,
  input  in_7,
  input  in_8,
  output out_9,
  output out_10,
  output out_11,
  output out_12
);

  or or_1 (out_9, in_1, in_2);
  or or_2 (out_10, in_3, in_4);
  or or_3 (out_11, in_5, in_6);
  or or_4 (out_12, in_7, in_8);
endmodule

module NOT_7404 (
  input  in_1,
  input  in_2,
  input  in_3,
  input  in_4,
  input  in_5,
  input  in_6,
  output out_7,
  output out_8,
  output out_9,
  output out_10,
  output out_11,
  output out_12
);

  not not_1 (out_7, in_1);
  not not_2 (out_8, in_2);
  not not_3 (out_9, in_3);
  not not_4 (out_10, in_4);
  not not_5 (out_11, in_5);
  not not_6 (out_12, in_6);
endmodule

module XOR_7486 (
  input  in_1,
  input  in_2,
  input  in_3,
  input  in_4,
  input  in_5,
  input  in_6,
  input  in_7,
  input  in_8,
  output out_9,
  output out_10,
  output out_11,
  output out_12
);

  xor xor_1 (out_9, in_1, in_2);
  xor xor_2 (out_10, in_3, in_4);
  xor xor_3 (out_11, in_5, in_6);
  xor xor_4 (out_12, in_7, in_8);
endmodule

module MUX_4x1 (
  input  I0,
  input  I1,
  input  I2,
  input  I3,
  input  S1,
  input  S0,
  output out_7
);

  wire and_1_out, and_2_out, and_3_out, and_4_out, not_1_out, not_2_out;

  not not_1 (not_1_out, S1);
  not not_2 (not_2_out, S0);
  and and_1 (and_1_out, I0, not_1_out, not_2_out);
  and and_2 (and_2_out, I1, not_1_out, S0);
  and and_3 (and_3_out, I2, S1, not_2_out);
  and and_4 (and_4_out, I3, S1, S0);
  or or_1 (out_7, and_1_out, and_2_out, and_3_out, and_4_out);
endmodule

module four_bit_adder_74283 (
  input  A1,
  input  B1,
  input  C,
  input  A2,
  input  B2,
  input  A3,
  input  B3,
  input  A4,
  input  B4,
  output S1,
  output S2,
  output S3,
  output S4,
  output CA
);

  wire and_1_out, and_2_out, and_3_out, and_4_out, and_5_out, and_6_out, and_7_out, and_8_out, or_1_out,
       or_2_out, or_3_out, xor_1_out, xor_2_out, xor_3_out, xor_4_out;

  xor xor_1 (xor_1_out, A1, B1);
  and and_1 (and_1_out, A1, B1);
  xor xor_2 (xor_2_out, A2, B2);
  and and_2 (and_2_out, A2, B2);
  xor xor_3 (xor_3_out, A3, B3);
  and and_3 (and_3_out, A3, B3);
  xor xor_4 (xor_4_out, A4, B4);
  and and_4 (and_4_out, A4, B4);
  and and_5 (and_5_out, xor_1_out, C);
  and and_6 (and_6_out, xor_2_out, or_1_out);
  xor xor_5 (S1, xor_1_out, C);
  xor xor_6 (S2, xor_2_out, or_1_out);
  and and_7 (and_7_out, xor_3_out, or_2_out);
  and and_8 (and_8_out, xor_4_out, or_3_out);
  or or_1 (or_1_out, and_5_out, and_1_out);
  or or_2 (or_2_out, and_6_out, and_2_out);
  xor xor_7 (S3, xor_3_out, or_2_out);
  or or_3 (or_3_out, and_7_out, and_3_out);
  xor xor_8 (S4, xor_4_out, or_3_out);
  or or_4 (CA, and_8_out, and_4_out);
endmodule

module ALU_1_bit (
  input  B,
  input  A,
  input  Bin,
  input  Cin,
  input  [2:0] in_5,
  output R,
  output Cout
);

  wire adder_1_out, and_1_out, multiplexer_1_out, nand_1_out, not_1_out, or_1_out, shifter_1_out,
       shifter_2_out, xnor_1_out, xor_1_out;

  not not_1 (not_1_out, B);
  Multiplexer multiplexer_1 (.in0(B), .in1(not_1_out), .out(multiplexer_1_out), .sel(Bin));
  and and_1 (and_1_out, A, B);
  or or_1 (or_1_out, A, B);
  Adder #(.width(1)) adder_1 (.a(A), .b(multiplexer_1_out), .out(adder_1_out), .cin(Cin), .cout(Cout));
  xor xor_1 (xor_1_out, A, B);
  nand nand_1 (nand_1_out, A, B);
  xnor xnor_1 (xnor_1_out, A, B);
  Shifter #(.width(1)) shifter_1 (.in(A), .\dist (B), .out(shifter_1_out));
  Shifter #(.shift("lr"), .width(1)) shifter_2 (.in(A), .\dist (B), .out(shifter_2_out));
  Multiplexer #(.select(3)) multiplexer_2 (
    .in0(and_1_out), .in1(or_1_out), .in2(adder_1_out), .in3(xor_1_out), .in4(nand_1_out), .in5(xnor_1_out),
    .in6(shifter_1_out), .in7(shifter_2_out), .out(R), .sel(in_5));
endmodule

module ALU_16_bit (
  input  [15:0] B,
  input  [15:0] A,
  input  Cin,
  input  Bin,
  input  [2:0] ALU_Op,
  output out_6,
  output [15:0] Result,
  output Cout
);

  wire [3:0] bit_extender_1_out;
  wire [15:0] adder_1_out, and_1_out, divider_1_out, multiplexer_1_out, multiplier_1_out, nand_1_out,
       not_1_out, or_1_out, shifter_1_out, xor_1_out;

  assign not_1_out = ~B;  // NOT_Gate not_1, 16 bits wide
  Multiplexer #(.width(16)) multiplexer_1 (.in0(B), .in1(not_1_out), .out(multiplexer_1_out), .sel(Bin));
  Bit_Extender #(.in_width(16), .out_width(4)) bit_extender_1 (.in(B), .out(bit_extender_1_out));
  assign and_1_out = A & B;  // AND_Gate and_1, 16 bits wide
  assign or_1_out = A | B;  // OR_Gate or_1, 16 bits wide
  Adder #(.width(16)) adder_1 (.a(A), .b(multiplexer_1_out), .out(adder_1_out), .cin(Cin), .cout(Cout));
  Multiplier #(.width(16)) multiplier_1 (.a(A), .b(B), .out(multiplier_1_out));  // open: cin, cout
  Divider #(.width(16)) divider_1 (.a(A), .b(B), .out(divider_1_out));  // open: upper, rem
  assign nand_1_out = ~(A & B);  // NAND_Gate nand_1, 16 bits wide
  assign xor_1_out = A ^ B;  // XOR_Gate xor_1, 16 bits wide
  Shifter #(.width(16)) shifter_1 (.in(A), .\dist (bit_extender_1_out), .out(shifter_1_out));
  Multiplexer #(.select(3), .width(16)) multiplexer_2 (
    .in0(and_1_out), .in1(or_1_out), .in2(adder_1_out), .in3(multiplier_1_out), .in4(divider_1_out),
    .in5(nand_1_out), .in6(xor_1_out), .in7(shifter_1_out), .out(Result), .sel(ALU_Op));
  nor nor_1 (out_6, Result[15], Result[14], Result[13], Result[12], Result[11], Result[10], Result[9], Result[8], Result[7], Result[6], Result[5], Result[4], Result[3], Result[2], Result[1], Result[0]);
endmodule

module ALU_16_bit_using_1_bit (
  input  [2:0] Op_Code,
  input  Cin,
  input  Bin,
  input  [15:0] A,
  input  [15:0] B,
  output [15:0] R,
  output Cout
);

  wire alu_1_bit_1_cout, alu_1_bit_2_cout, alu_1_bit_3_cout, alu_1_bit_4_cout, alu_1_bit_5_cout,
       alu_1_bit_6_cout, alu_1_bit_7_cout, alu_1_bit_8_cout, alu_1_bit_9_cout, alu_1_bit_10_cout,
       alu_1_bit_11_cout, alu_1_bit_12_cout, alu_1_bit_13_cout, alu_1_bit_14_cout, alu_1_bit_15_cout;

  ALU_1_bit alu_1_bit_1 (.A(A[0]), .Bin(Bin), .Cin(Cin), .in_5(Op_Code), .B(B[0]), .Cout(alu_1_bit_1_cout), .R(R[0]));
  ALU_1_bit alu_1_bit_2 (
    .A(A[1]), .Bin(Bin), .Cin(alu_1_bit_1_cout), .in_5(Op_Code), .B(B[1]), .Cout(alu_1_bit_2_cout), .R(R[1]));
  ALU_1_bit alu_1_bit_3 (
    .A(A[2]), .Bin(Bin), .Cin(alu_1_bit_2_cout), .in_5(Op_Code), .B(B[2]), .Cout(alu_1_bit_3_cout), .R(R[2]));
  ALU_1_bit alu_1_bit_4 (
    .A(A[3]), .Bin(Bin), .Cin(alu_1_bit_3_cout), .in_5(Op_Code), .B(B[3]), .Cout(alu_1_bit_4_cout), .R(R[3]));
  ALU_1_bit alu_1_bit_5 (
    .A(A[4]), .Bin(Bin), .Cin(alu_1_bit_4_cout), .in_5(Op_Code), .B(B[4]), .Cout(alu_1_bit_5_cout), .R(R[4]));
  ALU_1_bit alu_1_bit_6 (
    .A(A[5]), .Bin(Bin), .Cin(alu_1_bit_5_cout), .in_5(Op_Code), .B(B[5]), .Cout(alu_1_bit_6_cout), .R(R[5]));
  ALU_1_bit alu_1_bit_7 (
    .A(A[6]), .Bin(Bin), .Cin(alu_1_bit_6_cout), .in_5(Op_Code), .B(B[6]), .Cout(alu_1_bit_7_cout), .R(R[6]));
  ALU_1_bit alu_1_bit_8 (
    .A(A[7]), .Bin(Bin), .Cin(alu_1_bit_7_cout), .in_5(Op_Code), .B(B[7]), .Cout(alu_1_bit_8_cout), .R(R[7]));
  ALU_1_bit alu_1_bit_9 (
    .A(A[8]), .Bin(Bin), .Cin(alu_1_bit_8_cout), .in_5(Op_Code), .B(B[8]), .Cout(alu_1_bit_9_cout), .R(R[8]));
  ALU_1_bit alu_1_bit_10 (
    .A(A[9]), .Bin(Bin), .Cin(alu_1_bit_9_cout), .in_5(Op_Code), .B(B[9]), .Cout(alu_1_bit_10_cout), .R(R[9]));
  ALU_1_bit alu_1_bit_11 (
    .A(A[10]), .Bin(Bin), .Cin(alu_1_bit_10_cout), .in_5(Op_Code), .B(B[10]), .Cout(alu_1_bit_11_cout),
    .R(R[10]));
  ALU_1_bit alu_1_bit_12 (
    .A(A[11]), .Bin(Bin), .Cin(alu_1_bit_11_cout), .in_5(Op_Code), .B(B[11]), .Cout(alu_1_bit_12_cout),
    .R(R[11]));
  ALU_1_bit alu_1_bit_13 (
    .A(A[12]), .Bin(Bin), .Cin(alu_1_bit_12_cout), .in_5(Op_Code), .B(B[12]), .Cout(alu_1_bit_13_cout),
    .R(R[12]));
  ALU_1_bit alu_1_bit_14 (
    .A(A[13]), .Bin(Bin), .Cin(alu_1_bit_13_cout), .in_5(Op_Code), .B(B[13]), .Cout(alu_1_bit_14_cout),
    .R(R[13]));
  ALU_1_bit alu_1_bit_15 (
    .A(A[14]), .Bin(Bin), .Cin(alu_1_bit_14_cout), .in_5(Op_Code), .B(B[14]), .Cout(alu_1_bit_15_cout),
    .R(R[14]));
  ALU_1_bit alu_1_bit_16 (
    .A(A[15]), .Bin(Bin), .Cin(alu_1_bit_15_cout), .in_5(Op_Code), .B(B[15]), .Cout(Cout), .R(R[15]));
endmodule

module Register_File (
  input  [15:0] data_input,
  input  Write_enb,
  input  [3:0] Read_reg1,
  input  [3:0] Write_Reg,
  input  [3:0] Read_reg2,
  input  Clock,
  output [15:0] Read_Data1,
  output [15:0] Read_Data2
);

  wire and_1_out, and_2_out, and_3_out, and_4_out, and_5_out, and_6_out, and_7_out, and_8_out, and_9_out,
       and_10_out, and_11_out, and_12_out, and_13_out, and_14_out, and_15_out, and_16_out, decoder_1_out0,
       decoder_1_out1, decoder_1_out2, decoder_1_out3, decoder_1_out4, decoder_1_out5, decoder_1_out6,
       decoder_1_out7, decoder_1_out8, decoder_1_out9, decoder_1_out10, decoder_1_out11, decoder_1_out12,
       decoder_1_out13, decoder_1_out14, decoder_1_out15;
  wire [15:0] register_1_q, register_2_q, register_3_q, register_4_q, register_5_q, register_6_q,
       register_7_q, register_8_q, register_9_q, register_10_q, register_11_q, register_12_q, register_13_q,
       register_14_q, register_15_q, register_16_q;

  Decoder #(.select(4)) decoder_1 (
    .out0(decoder_1_out0), .out1(decoder_1_out1), .out2(decoder_1_out2), .out3(decoder_1_out3),
    .out4(decoder_1_out4), .out5(decoder_1_out5), .out6(decoder_1_out6), .out7(decoder_1_out7),
    .out8(decoder_1_out8), .out9(decoder_1_out9), .out10(decoder_1_out10), .out11(decoder_1_out11),
    .out12(decoder_1_out12), .out13(decoder_1_out13), .out14(decoder_1_out14), .out15(decoder_1_out15),
    .sel(Write_Reg));  // open: en
  and and_1 (and_1_out, decoder_1_out0, Write_enb);
  and and_2 (and_2_out, decoder_1_out1, Write_enb);
  and and_3 (and_3_out, decoder_1_out2, Write_enb);
  and and_4 (and_4_out, decoder_1_out3, Write_enb);
  and and_5 (and_5_out, decoder_1_out4, Write_enb);
  and and_6 (and_6_out, decoder_1_out5, Write_enb);
  and and_7 (and_7_out, decoder_1_out6, Write_enb);
  and and_8 (and_8_out, decoder_1_out7, Write_enb);
  and and_9 (and_9_out, decoder_1_out8, Write_enb);
  and and_10 (and_10_out, decoder_1_out9, Write_enb);
  and and_11 (and_11_out, decoder_1_out10, Write_enb);
  and and_12 (and_12_out, decoder_1_out11, Write_enb);
  and and_13 (and_13_out, decoder_1_out12, Write_enb);
  and and_14 (and_14_out, decoder_1_out13, Write_enb);
  and and_15 (and_15_out, decoder_1_out14, Write_enb);
  and and_16 (and_16_out, decoder_1_out15, Write_enb);
  Register #(.width(16)) register_1 (.D(data_input), .en(and_1_out), .Q(register_1_q), .clk(Clock));  // open: clr
  Register #(.width(16)) register_2 (.D(data_input), .en(and_2_out), .Q(register_2_q), .clk(Clock));  // open: clr
  Register #(.width(16)) register_3 (.D(data_input), .en(and_3_out), .Q(register_3_q), .clk(Clock));  // open: clr
  Register #(.width(16)) register_4 (.D(data_input), .en(and_4_out), .Q(register_4_q), .clk(Clock));  // open: clr
  Register #(.width(16)) register_5 (.D(data_input), .en(and_5_out), .Q(register_5_q), .clk(Clock));  // open: clr
  Register #(.width(16)) register_6 (.D(data_input), .en(and_6_out), .Q(register_6_q), .clk(Clock));  // open: clr
  Register #(.width(16)) register_7 (.D(data_input), .en(and_7_out), .Q(register_7_q), .clk(Clock));  // open: clr
  Register #(.width(16)) register_8 (.D(data_input), .en(and_8_out), .Q(register_8_q), .clk(Clock));  // open: clr
  Register #(.width(16)) register_9 (.D(data_input), .en(and_9_out), .Q(register_9_q), .clk(Clock));  // open: clr
  Register #(.width(16)) register_10 (.D(data_input), .en(and_10_out), .Q(register_10_q), .clk(Clock));  // open: clr
  Register #(.width(16)) register_11 (.D(data_input), .en(and_11_out), .Q(register_11_q), .clk(Clock));  // open: clr
  Register #(.width(16)) register_12 (.D(data_input), .en(and_12_out), .Q(register_12_q), .clk(Clock));  // open: clr
  Register #(.width(16)) register_13 (.D(data_input), .en(and_13_out), .Q(register_13_q), .clk(Clock));  // open: clr
  Register #(.width(16)) register_14 (.D(data_input), .en(and_14_out), .Q(register_14_q), .clk(Clock));  // open: clr
  Register #(.width(16)) register_15 (.D(data_input), .en(and_15_out), .Q(register_15_q), .clk(Clock));  // open: clr
  Register #(.width(16)) register_16 (.D(data_input), .en(and_16_out), .Q(register_16_q), .clk(Clock));  // open: clr
  Multiplexer #(.select(4), .width(16)) multiplexer_1 (
    .in0(register_1_q), .in1(register_2_q), .in2(register_3_q), .in3(register_4_q), .in4(register_5_q),
    .in5(register_6_q), .in6(register_7_q), .in7(register_8_q), .in8(register_9_q), .in9(register_10_q),
    .in10(register_11_q), .in11(register_12_q), .in12(register_13_q), .in13(register_14_q),
    .in14(register_15_q), .in15(register_16_q), .out(Read_Data2), .sel(Read_reg2));
  Multiplexer #(.select(4), .width(16)) multiplexer_2 (
    .in0(register_1_q), .in1(register_2_q), .in2(register_3_q), .in3(register_4_q), .in4(register_5_q),
    .in5(register_6_q), .in6(register_7_q), .in7(register_8_q), .in8(register_9_q), .in9(register_10_q),
    .in10(register_11_q), .in11(register_12_q), .in12(register_13_q), .in13(register_14_q),
    .in14(register_15_q), .in15(register_16_q), .out(Read_Data1), .sel(Read_reg1));
endmodule

module R_type (
  input  in_1,
  input  in_2,
  input  in_3,
  input  [2:0] in_4,
  input  in_5,
  output [3:0] OP_Code,
  output [3:0] Read_reg1,
  output [3:0] Read_reg2,
  output [3:0] Write_reg
);

  wire clock_1_out, clock_2_out;
  wire [15:0] adder_1_out, alu_16_bit_1_result, register_1_q, register_file_1_read_data1,
       register_file_1_read_data2;

  Clock clock_1 (.out(clock_1_out));
  Register #(.width(16)) register_1 (.D(adder_1_out), .clk(clock_1_out), .Q(register_1_q), .clr(in_3));  // open: en
  Adder #(.width(16)) adder_1 (.a(register_1_q), .b(16'h1), .out(adder_1_out));  // open: cin, cout
  ROM #(.addrWidth(16), .dataWidth(16)) rom_1 (.addr(register_1_q), .data({OP_Code, Read_reg1, Read_reg2, Write_reg}));
  Clock clock_2 (.out(clock_2_out));
  Register_File register_file_1 (
    .Write_Reg(Write_reg), .data_input(alu_16_bit_1_result), .Write_enb(in_5), .Clock(clock_2_out),
    .Read_reg2(Read_reg2), .Read_reg1(Read_reg1), .Read_Data2(register_file_1_read_data2),
    .Read_Data1(register_file_1_read_data1));
  ALU_16_bit alu_16_bit_1 (
    .Bin(in_2), .B(register_file_1_read_data2), .A(register_file_1_read_data1), .Cin(in_1), .ALU_Op(in_4),
    .Result(alu_16_bit_1_result));  // open: Cout, out_6

  // Notes on the sheet:
  //   contents of rom_1 (hex, n*v repeats v):
  //   1012 2345 3678
endmodule

module I_type (
  input  in_1,
  input  in_2,
  input  in_3,
  input  [2:0] in_4,
  input  in_5,
  output [3:0] OP_Code,
  output [3:0] Read_reg1,
  output [3:0] Write_reg,
  output [3:0] Imm
);

  wire clock_1_out;
  wire [15:0] adder_1_out, alu_16_bit_1_result, bit_extender_1_out, register_1_q, register_file_1_read_data1;

  Register #(.width(16)) register_1 (.D(adder_1_out), .clk(clock_1_out), .Q(register_1_q), .clr(in_3));  // open: en
  Adder #(.width(16)) adder_1 (.a(register_1_q), .b(16'h1), .out(adder_1_out));  // open: cin, cout
  ROM #(.addrWidth(16), .dataWidth(16)) rom_1 (.addr(register_1_q), .data({OP_Code, Read_reg1, Write_reg, Imm}));
  Clock clock_1 (.out(clock_1_out));
  Register_File register_file_1 (
    .Write_Reg(Write_reg), .data_input(alu_16_bit_1_result), .Write_enb(in_5), .Clock(clock_1_out),
    .Read_reg1(Read_reg1), .Read_Data1(register_file_1_read_data1));  // open: Read_reg2, Read_Data2
  assign bit_extender_1_out = {{12{Imm[3]}}, Imm};  // Bit_Extender bit_extender_1
  ALU_16_bit alu_16_bit_1 (
    .Bin(in_2), .B(bit_extender_1_out), .A(register_file_1_read_data1), .Cin(in_1), .ALU_Op(in_4),
    .Result(alu_16_bit_1_result));  // open: Cout, out_6

  // Notes on the sheet:
  //   contents of rom_1 (hex, n*v repeats v):
  //   123
endmodule

module Load (
  input  in_1,
  input  in_2,
  input  R,
  input  W,
  input  in_5,
  input  [2:0] in_6,
  input  in_7,
  output [3:0] OP_Code,
  output [3:0] Read_reg1,
  output [3:0] Write_reg,
  output [3:0] Imm
);

  wire clock_1_out;
  wire [15:0] adder_1_out, alu_16_bit_1_result, bit_extender_1_out, ram_1_dout, register_1_q,
       register_file_1_read_data1;

  Register #(.width(16)) register_1 (.D(adder_1_out), .clk(clock_1_out), .Q(register_1_q), .clr(in_5));  // open: en
  Adder #(.width(16)) adder_1 (.a(register_1_q), .b(16'h1), .out(adder_1_out));  // open: cin, cout
  ROM #(.addrWidth(16), .dataWidth(16)) rom_1 (.addr(register_1_q), .data({OP_Code, Read_reg1, Write_reg, Imm}));
  Clock clock_1 (.out(clock_1_out));
  Register_File register_file_1 (
    .Write_Reg(Write_reg), .data_input(ram_1_dout), .Write_enb(in_7), .Clock(clock_1_out),
    .Read_reg1(Read_reg1), .Read_Data1(register_file_1_read_data1));  // open: Read_reg2, Read_Data2
  assign bit_extender_1_out = {{12{Imm[3]}}, Imm};  // Bit_Extender bit_extender_1
  ALU_16_bit alu_16_bit_1 (
    .Bin(in_2), .B(bit_extender_1_out), .A(register_file_1_read_data1), .Cin(in_1), .ALU_Op(in_6),
    .Result(alu_16_bit_1_result));  // open: Cout, out_6
  RAM #(.addrWidth(16), .asyncread("true"), .dataWidth(16)) ram_1 (
    .addr(alu_16_bit_1_result), .we(W), .oe(R), .clk(clock_1_out), .dout(ram_1_dout));  // open: din

  // Notes on the sheet:
  //   contents of rom_1 (hex, n*v repeats v):
  //   123
endmodule

module Store (
  input  in_1,
  input  in_2,
  input  R,
  input  W,
  input  in_5,
  input  [2:0] in_6,
  input  in_7,
  output [3:0] OP_Code,
  output [3:0] Read_reg1,
  output [3:0] Write_reg,
  output [3:0] Imm
);

  wire clock_1_out;
  wire [15:0] adder_1_out, alu_16_bit_1_result, bit_extender_1_out, register_1_q, register_file_1_read_data1,
       register_file_1_read_data2;

  Register #(.width(16)) register_1 (.D(adder_1_out), .clk(clock_1_out), .Q(register_1_q), .clr(in_5));  // open: en
  Adder #(.width(16)) adder_1 (.a(register_1_q), .b(16'h1), .out(adder_1_out));  // open: cin, cout
  ROM #(.addrWidth(16), .dataWidth(16)) rom_1 (.addr(register_1_q), .data({OP_Code, Read_reg1, Write_reg, Imm}));
  Clock clock_1 (.out(clock_1_out));
  Register_File register_file_1 (
    .Write_enb(in_7), .Clock(clock_1_out), .Read_reg2(Write_reg), .Read_reg1(Read_reg1),
    .Read_Data2(register_file_1_read_data2), .Read_Data1(register_file_1_read_data1));  // open: Write_Reg, data_input
  assign bit_extender_1_out = {{12{Imm[3]}}, Imm};  // Bit_Extender bit_extender_1
  ALU_16_bit alu_16_bit_1 (
    .Bin(in_2), .B(bit_extender_1_out), .A(register_file_1_read_data1), .Cin(in_1), .ALU_Op(in_6),
    .Result(alu_16_bit_1_result));  // open: Cout, out_6
  RAM #(.addrWidth(16), .asyncread("true"), .dataWidth(16)) ram_1 (
    .addr(alu_16_bit_1_result), .we(W), .oe(R), .clk(clock_1_out), .din(register_file_1_read_data2));  // open: dout

  // Notes on the sheet:
  //   contents of rom_1 (hex, n*v repeats v):
  //   123
endmodule

module Merge (
  input  in_1
);

  wire CLK_out, control_1_alu_src, control_1_jump, control_1_lw, control_1_ram_to_reg, control_1_reg_dst,
       control_1_sub, control_1_sw, control_1_write_enb;
  wire [2:0] control_1_aluop;
  wire [3:0] multiplexer_2_out;
  wire [15:0] adder_1_out, alu_16_bit_1_result, bit_extender_1_out, bit_extender_2_out, multiplexer_1_out,
       multiplexer_3_out, multiplexer_4_out, ram_1_dout, register_1_q, register_file_1_read_data1,
       register_file_1_read_data2, rom_1_data;

  Multiplexer #(.width(16)) multiplexer_1 (
    .in0(adder_1_out), .in1(bit_extender_1_out), .out(multiplexer_1_out), .sel(control_1_jump));
  Register #(.width(16)) register_1 (.D(multiplexer_1_out), .clk(CLK_out), .Q(register_1_q), .clr(in_1));  // open: en
  Control control_1 (
    .OpCode(rom_1_data[15:12]), .Write_enb(control_1_write_enb), .Alu_src(control_1_alu_src),
    .AluOp(control_1_aluop), .Sub(control_1_sub), .lw(control_1_lw), .sw(control_1_sw),
    .ram_to_reg(control_1_ram_to_reg), .jump(control_1_jump), .Reg_dst(control_1_reg_dst));
  Adder #(.width(16)) adder_1 (.a(register_1_q), .b(16'h1), .out(adder_1_out));  // open: cin, cout
  ROM #(.addrWidth(16), .dataWidth(16)) rom_1 (.addr(register_1_q), .data(rom_1_data));
  Clock CLK (.out(CLK_out));
  assign bit_extender_1_out = {{4{rom_1_data[11]}}, rom_1_data[11:0]};  // Bit_Extender bit_extender_1
  Multiplexer #(.width(4)) multiplexer_2 (
    .in0(rom_1_data[3:0]), .in1(rom_1_data[7:4]), .out(multiplexer_2_out), .sel(control_1_reg_dst));
  Register_File register_file_1 (
    .Write_Reg(multiplexer_2_out), .data_input(multiplexer_4_out), .Write_enb(control_1_write_enb),
    .Clock(CLK_out), .Read_reg2(rom_1_data[7:4]), .Read_reg1(rom_1_data[11:8]),
    .Read_Data2(register_file_1_read_data2), .Read_Data1(register_file_1_read_data1));
  assign bit_extender_2_out = {{12{rom_1_data[3]}}, rom_1_data[3:0]};  // Bit_Extender bit_extender_2
  Multiplexer #(.width(16)) multiplexer_3 (
    .in0(register_file_1_read_data2), .in1(bit_extender_2_out), .out(multiplexer_3_out),
    .sel(control_1_alu_src));
  ALU_16_bit alu_16_bit_1 (
    .Bin(control_1_sub), .B(multiplexer_3_out), .A(register_file_1_read_data1), .Cin(control_1_sub),
    .ALU_Op(control_1_aluop), .Result(alu_16_bit_1_result));  // open: Cout, out_6
  RAM #(.addrWidth(16), .asyncread("true"), .dataWidth(16)) ram_1 (
    .addr(alu_16_bit_1_result), .we(control_1_sw), .oe(control_1_lw), .clk(CLK_out),
    .din(register_file_1_read_data2), .dout(ram_1_dout));
  Multiplexer #(.width(16)) multiplexer_4 (
    .in0(alu_16_bit_1_result), .in1(ram_1_dout), .out(multiplexer_4_out), .sel(control_1_ram_to_reg));
endmodule

module Control (
  input  [3:0] OpCode,
  output Reg_dst,
  output Write_enb,
  output Alu_src,
  output [2:0] AluOp,
  output Sub,
  output lw,
  output sw,
  output ram_to_reg,
  output jump
);

  wire and_1_out, and_2_out, and_3_out, and_4_out, and_5_out, and_6_out, and_7_out, and_8_out, and_9_out,
       and_10_out, and_11_out, and_12_out, and_13_out, and_14_out, not_1_out, not_2_out, not_3_out, not_4_out;

  not not_1 (not_1_out, OpCode[3]);
  not not_2 (not_2_out, OpCode[2]);
  not not_3 (not_3_out, OpCode[1]);
  not not_4 (not_4_out, OpCode[0]);
  and and_1 (and_1_out, not_1_out, OpCode[1], not_4_out);
  and and_2 (and_2_out, not_1_out, OpCode[2], OpCode[1]);
  and and_3 (and_3_out, OpCode[3], not_2_out, not_3_out);
  and and_4 (and_4_out, not_1_out, not_4_out);
  and and_5 (and_5_out, not_2_out, not_3_out);
  and and_6 (and_6_out, not_1_out, OpCode[2]);
  and and_7 (and_7_out, not_1_out, OpCode[1]);
  and and_8 (and_8_out, OpCode[3], not_2_out, not_3_out);
  and and_9 (and_9_out, not_1_out, not_2_out);
  and and_10 (and_10_out, not_1_out, OpCode[1]);
  and and_11 (and_11_out, not_1_out, OpCode[2], not_3_out, OpCode[0]);
  and and_12 (and_12_out, OpCode[3], not_2_out, not_3_out, not_4_out);
  and and_13 (and_13_out, not_1_out, not_2_out, not_3_out, OpCode[0]);
  and and_14 (and_14_out, not_1_out, OpCode[2], OpCode[1], OpCode[0]);
  and and_15 (lw, not_1_out, not_2_out, OpCode[1], not_4_out);
  and and_16 (sw, not_1_out, not_2_out, OpCode[1], OpCode[0]);
  and and_17 (ram_to_reg, not_1_out, not_2_out, OpCode[1], not_4_out);
  and and_18 (jump, OpCode[3], not_2_out, OpCode[1], not_4_out);
  or or_1 (Reg_dst, and_1_out, and_2_out, and_3_out);
  or or_2 (Write_enb, and_4_out, and_5_out, and_6_out);
  or or_3 (Alu_src, and_7_out, and_8_out);
  or or_4 (AluOp[1], and_9_out, and_10_out);
  or or_5 (AluOp[0], and_11_out, and_12_out);
  or or_6 (Sub, and_13_out, and_14_out);

  assign AluOp[2] = 1'b0;
endmodule

module pipelined_datapath (
  output [3:0] Opcode,
  output [3:0] Rs,
  output [3:0] Rt,
  output [3:0] Rd_offset,
  output [15:0] Read_data1,
  output [15:0] ALU_Result,
  output [15:0] Read_data2
);

  wire clck_out, control_1_alu_src, control_1_jump, control_1_lw, control_1_ram_to_reg, control_1_reg_dst,
       control_1_sub, control_1_sw, control_1_write_enb, register_7_q, register_9_q, register_10_q,
       register_11_q, register_12_q, register_13_q, register_17_q, register_18_q, register_19_q,
       register_20_q;
  wire [2:0] control_1_aluop, register_8_q;
  wire [3:0] multiplexer_1_out, register_6_q, register_16_q, register_23_q;
  wire [15:0] adder_1_out, alu_16_bit_using_1_bit_1_r, bit_extender_1_out, multiplexer_3_out, ram_1_dout,
       register_1_q, register_4_q, register_5_q, register_15_q, register_21_q, register_22_q,
       register_file_1_read_data1, register_file_1_read_data2, rom_1_data;

  Register #(.width(16)) register_1 (.D(adder_1_out), .clk(clck_out), .Q(register_1_q));  // open: en, clr
  Clock clck (.out(clck_out));
  Adder #(.width(16)) adder_1 (.a(register_1_q), .b(16'h1), .out(adder_1_out));  // open: cin, cout
  ROM #(.addrWidth(16), .dataWidth(16)) rom_1 (.addr(register_1_q), .data(rom_1_data));
  Register #(.width(16)) register_2 (.D(rom_1_data), .Q({Opcode, Rs, Rt, Rd_offset}), .clk(clck_out));  // open: en, clr
  Multiplexer #(.width(4)) multiplexer_1 (.in0(Rd_offset), .in1(Rt), .out(multiplexer_1_out), .sel(control_1_reg_dst));
  Register_File register_file_1 (
    .Write_Reg(register_23_q), .data_input(multiplexer_3_out), .Write_enb(control_1_write_enb),
    .Clock(clck_out), .Read_reg2(Rt), .Read_reg1(Rs), .Read_Data2(register_file_1_read_data2),
    .Read_Data1(register_file_1_read_data1));
  assign bit_extender_1_out = {{12{Rd_offset[3]}}, Rd_offset};  // Bit_Extender bit_extender_1
  Register #(.width(16)) register_3 (.D(register_file_1_read_data1), .Q(Read_data1), .clk(clck_out));  // open: en, clr
  Register #(.width(16)) register_4 (
    .D(register_file_1_read_data2), .Q(register_4_q), .clk(clck_out));  // open: en, clr
  Register #(.width(16)) register_5 (.D(bit_extender_1_out), .Q(register_5_q), .clk(clck_out));  // open: en, clr
  Register #(.width(4)) register_6 (.D(multiplexer_1_out), .Q(register_6_q), .clk(clck_out));  // open: en, clr
  Control control_1 (
    .OpCode(Opcode), .Write_enb(control_1_write_enb), .Alu_src(control_1_alu_src), .AluOp(control_1_aluop),
    .Sub(control_1_sub), .lw(control_1_lw), .sw(control_1_sw), .ram_to_reg(control_1_ram_to_reg),
    .jump(control_1_jump), .Reg_dst(control_1_reg_dst));
  Multiplexer #(.width(16)) multiplexer_2 (
    .in0(register_4_q), .in1(register_5_q), .out(Read_data2), .sel(register_7_q));
  Register #(.width(1)) register_7 (.D(control_1_alu_src), .Q(register_7_q), .clk(clck_out));  // open: en, clr
  Register #(.width(3)) register_8 (.D(control_1_aluop), .Q(register_8_q), .clk(clck_out));  // open: en, clr
  Register #(.width(1)) register_9 (.D(control_1_sub), .Q(register_9_q), .clk(clck_out));  // open: en, clr
  Register #(.width(1)) register_10 (.D(control_1_lw), .Q(register_10_q), .clk(clck_out));  // open: en, clr
  Register #(.width(1)) register_11 (.D(control_1_sw), .Q(register_11_q), .clk(clck_out));  // open: en, clr
  Register #(.width(1)) register_12 (.D(control_1_ram_to_reg), .Q(register_12_q), .clk(clck_out));  // open: en, clr
  Register #(.width(1)) register_13 (.D(control_1_jump), .Q(register_13_q), .clk(clck_out));  // open: en, clr
  ALU_16_bit_using_1_bit alu_16_bit_using_1_bit_1 (
    .Op_Code(register_8_q), .Cin(register_9_q), .Bin(register_13_q), .A(Read_data1), .B(Read_data2),
    .R(alu_16_bit_using_1_bit_1_r));  // open: Cout
  Register #(.width(16)) register_14 (.D(alu_16_bit_using_1_bit_1_r), .Q(ALU_Result), .clk(clck_out));  // open: en, clr
  Register #(.width(16)) register_15 (.D(register_4_q), .Q(register_15_q), .clk(clck_out));  // open: en, clr
  Register #(.width(4)) register_16 (.D(register_6_q), .Q(register_16_q), .clk(clck_out));  // open: en, clr
  Register #(.width(1)) register_17 (.D(register_10_q), .Q(register_17_q), .clk(clck_out));  // open: en, clr
  Register #(.width(1)) register_18 (.D(register_11_q), .Q(register_18_q), .clk(clck_out));  // open: en, clr
  Register #(.width(1)) register_19 (.D(register_12_q), .Q(register_19_q), .clk(clck_out));  // open: en, clr
  RAM #(.addrWidth(16), .dataWidth(16)) ram_1 (
    .addr(ALU_Result), .we(register_18_q), .oe(register_17_q), .din(register_15_q), .dout(ram_1_dout));  // open: clk
  Register #(.width(1)) register_20 (.D(register_19_q), .Q(register_20_q), .clk(clck_out));  // open: en, clr
  Register #(.width(16)) register_21 (.D(ALU_Result), .Q(register_21_q), .clk(clck_out));  // open: en, clr
  Register #(.width(16)) register_22 (.D(ram_1_dout), .Q(register_22_q), .clk(clck_out));  // open: en, clr
  Register #(.width(4)) register_23 (.D(register_16_q), .Q(register_23_q), .clk(clck_out));  // open: en, clr
  Multiplexer #(.width(16)) multiplexer_3 (
    .in0(register_21_q), .in1(register_22_q), .out(multiplexer_3_out), .sel(register_20_q));
endmodule
